# Fritzing sketch node_center (saved by Fritzing 0.9.0b)
perfboards: 1

parts:
  To_Sensor_Board1 = female pin header, 6 pins [form="♀ (female)"]
  XBee_with_regulator = XBee
  R6 = Resistor [tolerance=±20% resistance=4.7k package=THT]
  R7 = Resistor [tolerance=±20% resistance=4.7k package=THT]
  R8 = Resistor [tolerance=±5% resistance=4.7k package=THT]
  VCC3 = 4 x AAA Battery Mount
  U1 = Voltage Regulator - 3.3V [package="TO220 [THT]"]
  J1 = male pin header, 4 pins [form="♂ (male)"]
  Arduino1 = Arduino Mini (Rev5)

nets:
  N1: To_Sensor_Board1.pin1, R7.Pin_1, R8.Pin_1, U1.output_voltage, J1.pin1, Arduino1.5V
  GND: To_Sensor_Board1.pin2, XBee_with_regulator.GND, R6.Pin_1, VCC3.-, U1.GND, J1.pin2, Arduino1.GND
  N2: To_Sensor_Board1.pin3, Arduino1.A1
  N3: To_Sensor_Board1.pin4, Arduino1.A0
  N4: To_Sensor_Board1.pin5, R7.Pin_0, J1.pin3, Arduino1.A5
  N5: To_Sensor_Board1.pin6, R8.Pin_0, J1.pin4, Arduino1.A4
  N6: XBee_with_regulator.VCC, VCC3.+, U1.input_voltage
  N7: XBee_with_regulator.pin2, Arduino1.D1/RX, Arduino1.RX
  N8: XBee_with_regulator.pin3, Arduino1.D0/TX, Arduino1.TX
  N9: XBee_with_regulator.pin9, R6.Pin_0, Arduino1.D2
