# Fritzing sketch node_garden (saved by Fritzing 0.9.0b)
perfboards: 1

parts:
  Luminosity_Sensor = Color Sensor Breakout ADJD-S311
  To_Main_Board1 = male pin header, 6 pins [form="♂ (male)"]
  パーツ1 = HTU21D Breakout
  Moisture_Sensor_3 = male pin header, 4 pins [form="♂ (male)"]
  Moisture_Sensor_4 = male pin header, 4 pins [form="♂ (male)"]
  J1 = male pin header, 4 pins [form="♂ (male)"]
  J2 = male pin header, 4 pins [form="♂ (male)"]

nets:
  VCC: Luminosity_Sensor.VCC, To_Main_Board1.pin1, パーツ1.3.3V, Moisture_Sensor_3.pin1, Moisture_Sensor_4.pin1, J1.pin4, J2.pin4
  GND: Luminosity_Sensor.GND, To_Main_Board1.pin2, パーツ1.GND, Moisture_Sensor_3.pin2, Moisture_Sensor_4.pin2, J1.pin3, J2.pin3
  N1: Luminosity_Sensor.SCL, To_Main_Board1.pin5, パーツ1.SCL
  N2: Luminosity_Sensor.SDA, To_Main_Board1.pin6, パーツ1.SDA
  N3: To_Main_Board1.pin3, Moisture_Sensor_4.pin4, J2.pin1
  N4: To_Main_Board1.pin4, Moisture_Sensor_3.pin4, J1.pin1

custom parts:
  HTU21D Breakout: This is a breadboard friendly breakout board for the Measurement Specialties high-precision, low-power digital humidity sensor.
