# Fritzing sketch node_solar (saved by Fritzing 0.9.0b)
perfboards: 1

parts:
  パーツ3 = Humidity Temperature Sensor SHT15
  Luminosity_Sensor1 = Color Sensor Breakout ADJD-S311
  Moisture_Sensor_3 = female pin header, 4 pins [form="♀ (female)"]
  Moisture_Sensor_4 = female pin header, 4 pins [form="♀ (female)"]
  To_Main_Board1 = male pin header, 6 pins [form="♂ (male)"]
  Pressure_Sensor1 = MPL3115A2 [package=lga8]
  C2 = Ceramic Capacitor [capacitance=1µF package="100 mil [THT, multilayer]"]
  R5 = Resistor [tolerance=±20% resistance=4.7k package=THT]

nets:
  GND: パーツ3.GND, Luminosity_Sensor1.GND, Moisture_Sensor_3.pin1, Moisture_Sensor_4.pin1, To_Main_Board1.pin2, Pressure_Sensor1.GND, C2.0
  N1: パーツ3.SCL, Luminosity_Sensor1.SCL, To_Main_Board1.pin5, Pressure_Sensor1.SCL
  N2: パーツ3.SDA, Luminosity_Sensor1.SDA, To_Main_Board1.pin6, Pressure_Sensor1.SDA
  VCC: パーツ3.VCC, Luminosity_Sensor1.VCC, Moisture_Sensor_3.pin2, Moisture_Sensor_4.pin2, To_Main_Board1.pin1, Pressure_Sensor1.VDD, R5.Pin_0
  N3: Moisture_Sensor_3.pin4, To_Main_Board1.pin3
  N4: Moisture_Sensor_4.pin4, To_Main_Board1.pin4
  N5: Pressure_Sensor1.CAP, C2.1
  N6: Pressure_Sensor1.VDDIO, Pressure_Sensor1.INT2, R5.Pin_1
