# Fritzing sketch server (saved by Fritzing 0.9.0b)
circuit board: 8.46667cm x 5.64444cm

parts:
  Raspberry_Pi2 = Raspberry Pi B rev2
  XBee_Cordinater1 = XBee

nets:
  3V3: Raspberry_Pi2.3V3, Raspberry_Pi2.5V, XBee_Cordinater1.VCC
  GND: Raspberry_Pi2.GND, XBee_Cordinater1.GND
  N1: Raspberry_Pi2.GPIO_14, XBee_Cordinater1.pin3
  N2: Raspberry_Pi2.GPIO_15, XBee_Cordinater1.pin2
