# Fritzing sketch system (saved by Fritzing 0.9.0b)
circuit board: 8.66282cm x 5.92231cm
perfboards: 2

parts:
  XBee_EndDevice = XBee
  part = Arduino Nano (Rev3.0)
  part_2 = Humidity Temperature Sensor SHT15
  Luminosity_Sensor = Color Sensor Breakout ADJD-S311
  R2 = Resistor [tolerance=±20% resistance=4.7k package=THT]
  R3 = Resistor [tolerance=±5% resistance=4.7k package=THT]
  C1 = Ceramic Capacitor [capacitance=1µF package="100 mil [THT, multilayer]"]
  R4 = Resistor [tolerance=±20% resistance=4.7k package=THT]
  VCC1 = Battery block 9V
  Pressure_Sensor = MPL3115A2 [package=lga8]
  To_Sensor_Board = female pin header, 6 pins [form="♀ (female)"]
  Moisture_Sensor_1 = female pin header, 4 pins [form="♀ (female)"]
  Moisture_Sensor_2 = female pin header, 4 pins [form="♀ (female)"]
  To_Main_Board = male pin header, 6 pins [form="♂ (male)"]
  part_3 = Raspberry Pi B rev2
  R5 = Resistor [tolerance=±20% resistance=4.7k package=THT]
  XBee_Cordinater = XBee

nets:
  VCC: XBee_EndDevice.VCC, part.5V
  N1: XBee_EndDevice.pin2, part.D0/RX
  N2: XBee_EndDevice.pin3, part.D1/TX
  N3: XBee_EndDevice.pin9, part.D2, R5.Pin_0
  GND: XBee_EndDevice.GND, part.GND, VCC1.-, To_Sensor_Board.pin2, R5.Pin_1
  N4: part.VIN, VCC1.+
  N5: part.A7, To_Sensor_Board.pin3
  N6: part.A6, To_Sensor_Board.pin4
  N7: part.A5, R2.Pin_0, To_Sensor_Board.pin5
  N8: part.A4, R3.Pin_0, To_Sensor_Board.pin6
  N9: part.3V3, R2.Pin_1, R3.Pin_1, To_Sensor_Board.pin1
  GND_2: part_2.GND, Luminosity_Sensor.GND, C1.0, Pressure_Sensor.GND, Moisture_Sensor_1.pin1, Moisture_Sensor_2.pin1, To_Main_Board.pin2
  N10: part_2.SCL, Luminosity_Sensor.SCL, Pressure_Sensor.SCL, To_Main_Board.pin5
  N11: part_2.SDA, Luminosity_Sensor.SDA, Pressure_Sensor.SDA, To_Main_Board.pin6
  VCC_2: part_2.VCC, Luminosity_Sensor.VCC, R4.Pin_0, Pressure_Sensor.VDD, Moisture_Sensor_1.pin2, Moisture_Sensor_2.pin2, To_Main_Board.pin1
  N12: C1.1, Pressure_Sensor.CAP
  N13: R4.Pin_1, Pressure_Sensor.VDDIO, Pressure_Sensor.INT2
  N14: Moisture_Sensor_1.pin4, To_Main_Board.pin3
  N15: Moisture_Sensor_2.pin4, To_Main_Board.pin4
  5V: part_3.5V, XBee_Cordinater.VCC
  GND_3: part_3.GND, XBee_Cordinater.GND
  N16: part_3.GPIO_14, XBee_Cordinater.pin3
  N17: part_3.GPIO_15, XBee_Cordinater.pin2
